// Digital circuit instruction_decoder.dig as structural Verilog
module instruction_decoder (
  input  [15:0] Instr,
  output [3:0] Opcode,
  output RegDest,
  output RegSrc,
  output [9:0] Imm
);


  assign Imm = Instr[9:0];
  assign Opcode = Instr[15:12];
  assign RegDest = Instr[11];
  assign RegSrc = Instr[10];
endmodule

/* Test case:
Instr  Opcode RegDest RegSrc Imm
0x0000 0x0    0       0      0x000
0x1405 0x1    0       1      0x005
0x280A 0x2    1       0      0x00A
0xFFAF 0xF    1       1      0x3AF
*/
