// Digital circuit pc.dig as structural Verilog
module pc (
  input  Load,
  input  CLR,
  input  CLK,
  input  [15:0] JumpTarget,
  output [15:0] PC_Out
);

  wire or_1_out;
  wire [15:0] add_1_s, multiplexer_1_out;

  Register #(.Bits(16)) register_1 (.D(multiplexer_1_out), .C(CLK), .en(1'b1), .Q(PC_Out));
  Add #(.Bits(16)) add_1 (.a(PC_Out), .b(16'h1), .c_i(1'b0), .s(add_1_s));  // open: c_o
  Multiplexer #(.Bits(16)) multiplexer_1 (.sel(or_1_out), .in_0(add_1_s), .in_1(JumpTarget), .out(multiplexer_1_out));
  or or_1 (or_1_out, Load, CLR);
endmodule

/* Test case:
CLR Load JumpTarget CLK PC_Out
1   0    0x0000     0   0x0000
1   0    0x0000     C   0x0000
0   0    0x0000     C   0x0001
0   0    0x0000     C   0x0002
0   0    0x0000     C   0x0003
0   1    0x0050     C   0x0050
0   0    0x0000     C   0x0051
1   0    0x0000     C   0x0000
*/
